# Fritzing sketch Circuit (saved by Fritzing 0.9.3b)

parts:
  Part1 = Arduino Uno (Rev3)
  Part2 = Bluetooth HC-05 Macho
  DEVICE1 = smd LED [color="Red (633nm)" package="0805 [SMD]"]
  DEVICE2 = smd LED [color="Blue (430nm)" package="0805 [SMD]"]
  DEVICE3 = smd LED [color="Green (555nm)" package="0805 [SMD]"]
  R1 = Resistor [tolerance=±5% resistance=220 package="0603 [SMD]"]  # not connected
  R3 = Resistor [tolerance=±5% resistance=220 package="0603 [SMD]"]  # not connected
  R4 = Resistor [tolerance=±5% resistance=220 package="0603 [SMD]"]  # not connected

nets:
  N1: Part1.D8, DEVICE3.anode
  N2: Part1.D12/MISO, DEVICE2.anode
  N3: Part1.D13/SCK, DEVICE1.anode
  GND: Part1.GND, Part2.GND
  N4: Part1.D0/RX, Part2.TXD
  N5: Part1.D1/TX, Part2.RXD
  5V: Part1.5V, Part2.VCC

// code stored in the sketch: bluetooth_arduino.ino
string Incoming_value = "";

void setup()
{
  Serial.begin(9600);
  pinMode(13, OUTPUT);
  pinMode(12, OUTPUT);
  pinMode(8, OUTPUT);
}

void loop()
{
  if(Serial.available() > 0)
  {
    Incoming_value += Serial.read();
    Serial.print(Incoming_value);
    Serial.print("\n");
    //Appliance 1
    if(Incoming_value == "11")
      digitalWrite(13, HIGH);
    else if(Incoming_value == "10")
      digitalWrite(13, LOW);
    //Appliance 2
    else if(Incoming_value == "21")
      digitalWrite(12, HIGH);
    else if(Incoming_value == "20")
      digitalWrite(12, LOW);
    //Appliance 3
    else if(Incoming_value == "31")
      digitalWrite(8, HIGH);
    else if(Incoming_value == "30")
      digitalWrite(8, LOW);
  }
}
